# Fritzing sketch ass6 (saved by Fritzing 0.9.4)
breadboards: 1

parts:
  Part1 = Arduino Ethernet Shield (Rev3)
  R1 = Resistor [tolerance=±5% resistance=10k package=THT]
  R2 = Resistor [tolerance=±5% resistance=10k package=THT]
  R3 = Resistor [tolerance=±5% resistance=100k package=THT]
  R4 = Resistor [tolerance=±5% resistance=100k package=THT]
  R5 = Resistor [tolerance=±5% resistance=100k package=THT]
  R6 = Resistor [tolerance=±5% resistance=100k package=THT]
  R7 = Trimmer Potentiometer [maximum_resistance=10kΩ package=THT]
  R10 = Trimmer Potentiometer [maximum_resistance=50kΩ package=THT]
  U2 = LM124-324 Quad Opamp [package="DIP (Dual Inline)"]
  R11 = Temperature Sensor (Thermistor) [thermistor_type=NTC package=THT]

nets:
  N1: Part1.GND, R3.Pin_0, R7.leg1, R10.leg1, U2.VCC-, R11.pin_1
  N2: Part1.AREF, R7.wiper
  N3: Part1.A0, R5.Pin_0, U2.1OUT
  N4: Part1.5V, R1.Pin_0, R2.Pin_0, R7.leg2, U2.VCC+
  N5: R1.Pin_1, R6.Pin_1, R11.pin_0
  N6: R2.Pin_1, R4.Pin_0, R10.wiper
  N7: R3.Pin_1, R4.Pin_1, U2.1IN+
  N8: R5.Pin_1, R6.Pin_0, U2.1IN-
